// Logisim project 2.b.circ as structural Verilog: 2 circuits, main circuit main
module main (
  input  [3:0] BCD8421,
  output [3:0] BCD8421_1_4aded82b,
  output Y3,
  output Y3_2,
  output Y3_3,
  output Y3_4
);

  wire and_1_out, and_2_out, and_3_out, not_1_out, not_2_out, not_4_out;

  // Probe on BCD8421
  not not_1 (not_1_out, BCD8421[3]);
  not not_2 (not_2_out, BCD8421[2]);
  not not_3 (BCD8421_1_4aded82b[1], BCD8421[1]);
  not not_4 (not_4_out, BCD8421[0]);
  and and_1 (and_1_out, BCD8421[2], BCD8421[1]);
  or or_1 (BCD8421_1_4aded82b[3], BCD8421[3], and_1_out);
  and and_2 (and_2_out, not_2_out, BCD8421[1]);
  and and_3 (and_3_out, BCD8421[2], BCD8421_1_4aded82b[1]);
  or or_2 (BCD8421_1_4aded82b[2], and_2_out, and_3_out);
  // Probe on {BCD8421_1_4aded82b[3:1], BCD8421[0]}

  assign BCD8421_1_4aded82b[0] = BCD8421[0];
  assign Y3 = BCD8421_1_4aded82b[3];
  assign Y3_2 = BCD8421_1_4aded82b[2];
  assign Y3_3 = BCD8421_1_4aded82b[1];
  assign Y3_4 = BCD8421[0];

  // Notes on the sheet:
  //   B
  //   C
  //   A
  //   !A
  //   D
  //   !B
  //   !C
  //   !D
endmodule

module main_f_eac2d9ec (
  input  [7:0] in_1,
  input  [7:0] in_2,
  output [7:0] out_3
);

  wire main_1_p3, main_1_p6, main_2_p6, main_3_p6, main_4_p6, main_5_p6, main_6_p6, main_7_p6;

  // Probe on in_1
  // Probe on in_2
  // main main_1: pin names not known; wires that end beside it: in_1[0], in_2[0], main_1_p3, in_1[1], in_2[1], main_1_p6, out_3[0], main_1_p3
  // main main_2: pin names not known; wires that end beside it: in_1[1], in_2[1], main_1_p6, in_1[2], in_2[2], main_2_p6, out_3[1], main_1_p6
  // main main_3: pin names not known; wires that end beside it: in_1[2], in_2[2], main_2_p6, in_1[3], in_2[3], main_3_p6, out_3[2], main_2_p6
  // main main_4: pin names not known; wires that end beside it: in_1[3], in_2[3], main_3_p6, in_1[4], in_2[4], main_4_p6, out_3[3], main_3_p6
  // main main_5: pin names not known; wires that end beside it: in_1[4], in_2[4], main_4_p6, in_1[5], in_2[5], main_5_p6, out_3[4], main_4_p6
  // main main_6: pin names not known; wires that end beside it: in_1[5], in_2[5], main_5_p6, in_1[6], in_2[6], main_6_p6, out_3[5], main_5_p6
  // main main_7: pin names not known; wires that end beside it: in_1[6], in_2[6], main_6_p6, in_1[7], in_2[7], main_7_p6, out_3[6], main_6_p6
  // main main_8: pin names not known; wires that end beside it: in_1[7], in_2[7], main_7_p6, main_1_p3, out_3[7], main_7_p6
  // Probe on out_3
endmodule
