// Logisim project ОДС.circ as structural Verilog: 1 circuit, main circuit main
module main (
  input  [7:0] A,
  input  [7:0] B,
  input  [7:0] C,
  output [7:0] out_4,
  output [7:0] out_5,
  output [7:0] out_6,
  output [7:0] out_7,
  output [7:0] out_8
);

  wire and_1_out, and_2_out, and_3_out, and_4_out, and_5_out, and_6_out, and_7_out, and_8_out, and_9_out,
       and_10_out, and_11_out, and_12_out, and_13_out, and_14_out, and_15_out, and_16_out, and_17_out,
       and_18_out, and_19_out, and_20_out, and_21_out, and_22_out, and_23_out, and_24_out, and_25_out,
       and_26_out, and_27_out, and_28_out, and_29_out, and_30_out, and_31_out, E0, E1, E2, E3, E4, E5, E6,
       E7, or_2_out, or_3_out, or_4_out, or_5_out, or_6_out, or_7_out, or_8_out, xor_1_out, xor_2_out,
       xor_3_out, xor_4_out, xor_5_out, xor_6_out, xor_7_out, xor_8_out, xor_10_out, xor_11_out, xor_12_out,
       xor_13_out, xor_14_out, xor_15_out, xor_16_out;

  and and_1 (and_1_out, B[0], C[0]);
  and and_2 (and_2_out, A[0], C[0]);
  and and_3 (and_3_out, A[0], B[0]);
  and and_4 (and_4_out, B[1], C[1]);
  and and_5 (and_5_out, A[1], C[1]);
  and and_6 (and_6_out, A[1], B[1]);
  and and_7 (and_7_out, B[2], C[2]);
  and and_8 (and_8_out, A[2], C[2]);
  and and_9 (and_9_out, A[2], B[2]);
  and and_10 (and_10_out, B[3], C[3]);
  and and_11 (and_11_out, A[3], C[3]);
  and and_12 (and_12_out, A[3], B[3]);
  and and_13 (and_13_out, B[4], C[4]);
  and and_14 (and_14_out, A[4], C[4]);
  and and_15 (and_15_out, A[4], B[4]);
  xor xor_1 (xor_1_out, B[0], C[0]);
  xor xor_2 (xor_2_out, B[1], C[1]);
  xor xor_3 (xor_3_out, B[2], C[2]);
  xor xor_4 (xor_4_out, B[3], C[3]);
  xor xor_5 (xor_5_out, B[4], C[4]);
  xor xor_6 (xor_6_out, B[5], C[5]);
  and and_16 (and_16_out, B[5], C[5]);
  and and_17 (and_17_out, A[5], C[5]);
  and and_18 (and_18_out, A[5], B[5]);
  xor xor_7 (xor_7_out, B[6], C[6]);
  and and_19 (and_19_out, B[6], C[6]);
  and and_20 (and_20_out, A[6], C[6]);
  and and_21 (and_21_out, A[6], B[6]);
  xor xor_8 (xor_8_out, B[7], C[7]);
  and and_22 (and_22_out, B[7], C[7]);
  and and_23 (and_23_out, A[7], C[7]);
  and and_24 (and_24_out, A[7], B[7]);
  xor xor_9 (out_7[0], xor_1_out, A[0]);
  or or_1 (E0, and_1_out, and_2_out, and_3_out);
  xor xor_10 (xor_10_out, xor_2_out, A[1]);
  or or_2 (or_2_out, and_4_out, and_5_out, and_6_out);
  xor xor_11 (xor_11_out, xor_3_out, A[2]);
  or or_3 (or_3_out, and_7_out, and_8_out, and_9_out);
  xor xor_12 (xor_12_out, xor_4_out, A[3]);
  or or_4 (or_4_out, and_10_out, and_11_out, and_12_out);
  xor xor_13 (xor_13_out, xor_5_out, A[4]);
  or or_5 (or_5_out, and_13_out, and_14_out, and_15_out);
  xor xor_14 (xor_14_out, xor_6_out, A[5]);
  or or_6 (or_6_out, and_16_out, and_17_out, and_18_out);
  xor xor_15 (xor_15_out, xor_7_out, A[6]);
  or or_7 (or_7_out, and_19_out, and_20_out, and_21_out);
  xor xor_16 (xor_16_out, xor_8_out, A[7]);
  or or_8 (or_8_out, and_22_out, and_23_out, and_24_out);
  xor xor_17 (out_7[1], xor_10_out, E0);
  and and_25 (and_25_out, E0, xor_10_out);
  xor xor_18 (out_7[2], xor_11_out, E1);
  and and_26 (and_26_out, E1, xor_11_out);
  xor xor_19 (out_7[3], xor_12_out, E2);
  and and_27 (and_27_out, E2, xor_12_out);
  xor xor_20 (out_7[4], xor_13_out, E3);
  and and_28 (and_28_out, E3, xor_13_out);
  xor xor_21 (out_7[5], xor_14_out, E4);
  and and_29 (and_29_out, E4, xor_14_out);
  xor xor_22 (out_7[6], xor_15_out, E5);
  and and_30 (and_30_out, E5, xor_15_out);
  xor xor_23 (out_7[7], xor_16_out, E6);
  and and_31 (and_31_out, E6, xor_16_out);
  or or_9 (E1, and_25_out, or_2_out);
  or or_10 (E2, and_26_out, or_3_out);
  or or_11 (E3, and_27_out, or_4_out);
  or or_12 (E4, and_28_out, or_5_out);
  or or_13 (E5, and_29_out, or_6_out);
  or or_14 (E6, and_30_out, or_7_out);
  or or_15 (E7, and_31_out, or_8_out);

  assign out_4 = A;
  assign out_5 = B;
  assign out_6 = C;
  assign out_8 = out_7;

  // Other names for the same wires on the sheet: S0 = out_7[0]; S1 = out_7[1]; S2 = out_7[2]; S3 = out_7[3];
  //   S4 = out_7[4]; S5 = out_7[5]; S6 = out_7[6]; S7 = out_7[7]
endmodule
